// Logisim project program1.circ as structural Verilog: 1 circuit, main circuit main
module main (
  input  in_1,
  input  in_2,
  input  in_3,
  input  in_4,
  input  in_5,
  input  in_6,
  input  in_7,
  output out_8,
  output out_9,
  output out_10,
  output out_11
);

  or or_1 (out_8, in_1, in_2);
  and and_1 (out_9, in_3, in_4);
  not not_1 (out_10, in_5);
  xor xor_1 (out_11, in_6, in_7);
endmodule
