// Logisim project program15.circ as structural Verilog: 1 circuit, main circuit main
module main (
  input  in_1,
  input  in_2,
  input  in_3,
  input  in_4,
  input  in_5,
  input  in_6,
  input  in_7,
  output out_8,
  output out_9,
  output out_10,
  output out_11,
  output out_12,
  output out_13
);

  J_K_Flip_Flop j_k_ff_1 (.J(in_1), .clk(in_2), .K(in_3), .Q(out_8), .Qn(out_9));  // open: preset, en, reset
  D_Flip_Flop d_ff_1 (.clk(in_4), .D(in_5), .Q(out_10), .Qn(out_11));  // open: preset, en, reset
  T_Flip_Flop t_ff_1 (.clk(in_6), .T(in_7), .Q(out_12), .Qn(out_13));  // open: preset, reset, en
endmodule
