// Logisim project program18.circ as structural Verilog: 1 circuit, main circuit main
module main (
  input  in_1,
  input  in_2
);

  wire and_1_out, and_2_out, and_3_out, and_4_out, clock_1_out, d_ff_1_q, d_ff_1_qn, d_ff_2_q, d_ff_2_qn,
       not_1_out, or_1_out, or_2_out;

  Clock clock_1 (.out(clock_1_out));
  not not_1 (not_1_out, in_1);
  D_Flip_Flop d_ff_1 (.clk(clock_1_out), .D(in_2), .Q(d_ff_1_q), .Qn(d_ff_1_qn));  // open: preset, en, reset
  and and_1 (and_1_out, not_1_out, d_ff_1_q);
  and and_2 (and_2_out, in_1, d_ff_1_qn);
  or or_1 (or_1_out, and_1_out, and_2_out);
  D_Flip_Flop d_ff_2 (.clk(clock_1_out), .D(or_1_out), .Q(d_ff_2_q), .Qn(d_ff_2_qn));  // open: preset, en, reset
  and and_3 (and_3_out, and_1_out, d_ff_2_q);
  and and_4 (and_4_out, d_ff_2_qn, and_2_out);
  or or_2 (or_2_out, and_3_out, and_4_out);
  D_Flip_Flop d_ff_3 (.clk(clock_1_out), .D(or_2_out));  // open: Q, Qn, preset, en, reset
endmodule
