// Logisim project program3.circ as structural Verilog: 1 circuit, main circuit main
module main (
  input  in_1,
  input  in_2,
  input  in_3,
  input  in_4,
  input  in_5,
  output out_6,
  output out_7,
  output out_8
);

  wire nor_1_out, nor_2_out, nor_3_out;

  nor nor_1 (nor_1_out, in_1, in_2);
  nor nor_2 (nor_2_out, in_3, in_3);
  nor nor_3 (nor_3_out, in_4, in_4);
  nor nor_4 (out_8, in_5, in_5);
  nor nor_5 (out_6, nor_1_out, nor_1_out);
  nor nor_6 (out_7, nor_2_out, nor_3_out);
endmodule
